// Logisim project scematics.circ as structural Verilog: 2 circuits, main circuit main
module main (
);

  wire and_1_out, not_1_out, Reset_out, w65c02s_expert_1_p5, w65c02s_expert_1_p6;
  wire [7:0] iolatch_1_out_3, w65c02s_expert_1_p8, w65c02s_expert_1_p9;
  wire [15:8] w65c02s_expert_1_p4;

  LED led_1 (.in(iolatch_1_out_3[0]));
  LED led_2 (.in(iolatch_1_out_3[1]));
  LED led_3 (.in(iolatch_1_out_3[2]));
  LED led_4 (.in(iolatch_1_out_3[3]));
  LED led_5 (.in(iolatch_1_out_3[4]));
  LED led_6 (.in(iolatch_1_out_3[5]));
  LED led_7 (.in(iolatch_1_out_3[6]));
  LED led_8 (.in(iolatch_1_out_3[7]));
  not not_1 (not_1_out, w65c02s_expert_1_p4[15]);
  Button Reset (.out(Reset_out));
  // W65C02S__Expert w65c02s_expert_1: pin names not known; wires that end beside it: 1'b1, 1'b1, 1'b1, w65c02s_expert_1_p4[8], w65c02s_expert_1_p5, w65c02s_expert_1_p6, 1'b1, w65c02s_expert_1_p8, {w65c02s_expert_1_p4, w65c02s_expert_1_p9}
  not not_2 (w65c02s_expert_1_p5, Reset_out);
  IOLatch iolatch_1 (.in_1(w65c02s_expert_1_p9), .in_2(and_1_out), .out_3(iolatch_1_out_3));
  and and_1 (and_1_out, w65c02s_expert_1_p4[8], w65c02s_expert_1_p4[9], w65c02s_expert_1_p4[10], w65c02s_expert_1_p4[11], w65c02s_expert_1_p4[12], w65c02s_expert_1_p4[13], w65c02s_expert_1_p4[14], not_1_out);
  ROM #(.addrWidth(15)) rom_1 (
    .addr({w65c02s_expert_1_p4[14:8], w65c02s_expert_1_p9}), .data(w65c02s_expert_1_p8),
    .sel(w65c02s_expert_1_p4[15]));
  Clock clock_1 (.out(w65c02s_expert_1_p6));

  // Notes on the sheet:
  //   IO Latch, this can be reaplaced with a VIA
  //   A 32K rom for storing the program for the computer
  //   contents of rom_1 (hex, n*v repeats v):
  //   a9 ff 8d 2 60 a9 55 8d 0 7f a9 55 8d ff 7f 4c 5 80 32746*ea 0 80 ea ea
endmodule

module IOLatch (
  input  [7:0] in_1,
  input  in_2,
  output [7:0] out_3
);

  D_Flip_Flop d_ff_1 (.clk(in_2), .D(in_1[0]), .Q(out_3[0]));  // open: Qn, preset, en, reset
  D_Flip_Flop d_ff_2 (.clk(in_2), .D(in_1[1]), .Q(out_3[1]));  // open: Qn, preset, en, reset
  D_Flip_Flop d_ff_3 (.clk(in_2), .D(in_1[2]), .Q(out_3[2]));  // open: Qn, preset, en, reset
  D_Flip_Flop d_ff_4 (.clk(in_2), .D(in_1[3]), .Q(out_3[3]));  // open: Qn, preset, en, reset
  D_Flip_Flop d_ff_5 (.clk(in_2), .D(in_1[4]), .Q(out_3[4]));  // open: Qn, preset, en, reset
  D_Flip_Flop d_ff_6 (.clk(in_2), .D(in_1[5]), .Q(out_3[5]));  // open: Qn, preset, en, reset
  D_Flip_Flop d_ff_7 (.clk(in_2), .D(in_1[6]), .Q(out_3[6]));  // open: Qn, preset, en, reset
  D_Flip_Flop d_ff_8 (.clk(in_2), .D(in_1[7]), .Q(out_3[7]));  // open: Qn, preset, en, reset
endmodule
